// Logisim project FLIP8_TTL.circ as structural Verilog: 1 circuit, main circuit main
module main (
);

  wire CKL, COUNT_OWR, n7_segment_display_1_p1, n7_segment_display_2_p1, n7_segment_display_3_p1,
       n74161_1_pin1, n74161_1_pin7, n74161_1_pin8, n74161_1_pin10, n74161_1_pin16, n74161_2_pin8, not_1_out,
       RESET;
  wire [7:0] n74161_2_pin3, n74161_2_pin14;

  Button button_1 (.out(COUNT_OWR));
  Button button_2 (.out(RESET));
  Clock clock_1 (.out(CKL));
  not not_1 (not_1_out, COUNT_OWR);
  _74161 #(.ShowInternalStructure("true"), .VccGndPorts("true")) u_74161_1 (
    .pin1(n74161_1_pin1), .pin2(CKL), .pin3(n74161_2_pin3[4]), .pin4(n74161_2_pin3[5]),
    .pin5(n74161_2_pin3[6]), .pin6(n74161_2_pin3[7]), .pin7(n74161_1_pin7), .pin8(n74161_1_pin8),
    .pin16(n74161_1_pin16), .pin14(n74161_2_pin14[4]), .pin13(n74161_2_pin14[5]), .pin12(n74161_2_pin14[6]),
    .pin11(n74161_2_pin14[7]), .pin10(n74161_1_pin10), .pin9(not_1_out));  // open: pin15
  not not_2 (n74161_1_pin1, RESET);
  _74161 #(.ShowInternalStructure("true"), .VccGndPorts("true")) u_74161_2 (
    .pin1(n74161_1_pin1), .pin2(CKL), .pin3(n74161_2_pin3[0]), .pin4(n74161_2_pin3[1]),
    .pin5(n74161_2_pin3[2]), .pin6(n74161_2_pin3[3]), .pin7(n74161_1_pin7), .pin8(n74161_2_pin8),
    .pin16(n74161_1_pin7), .pin15(n74161_1_pin10), .pin14(n74161_2_pin14[0]), .pin13(n74161_2_pin14[1]),
    .pin12(n74161_2_pin14[2]), .pin11(n74161_2_pin14[3]), .pin10(n74161_1_pin7), .pin9(not_1_out));
  // _7_Segment_Display 7_segment_display_1: pin names not known; wires that end beside it: n7_segment_display_1_p1, n7_segment_display_1_p1
  // BCD_to_7_Segment_decoder bcd_to_7_segment_decoder_1: pin names not known
  // Binary_to_BCD_converter #(.binvalue(8)) binary_to_bcd_converter_1: pin names not known; wires that end beside it: n74161_2_pin14
  // _7_Segment_Display 7_segment_display_2: pin names not known; wires that end beside it: n7_segment_display_2_p1, n7_segment_display_2_p1
  // _7_Segment_Display 7_segment_display_3: pin names not known; wires that end beside it: n7_segment_display_3_p1, n7_segment_display_3_p1
  // BCD_to_7_Segment_decoder bcd_to_7_segment_decoder_2: pin names not known
  // BCD_to_7_Segment_decoder bcd_to_7_segment_decoder_3: pin names not known
  // also tied to GND on the sheet: {n74161_1_pin8, n74161_2_pin8}
  // also tied to VCC on the sheet: {n74161_1_pin16, n74161_1_pin7}
endmodule
